# Fritzing sketch Commande Aspi_v2 (saved by Fritzing 0.9.4)
circuit board: 13cm x 9cm
breadboards: 1

parts:
  Nano_Motor_Drive = Arduino Nano (Rev3.0) (ICSP)
  Power = female pin header, 2 pins [form="♀ (female)"]
  OK = LED - 5mm [color="Green (555nm)" package="5 mm [THT]"]
  R1 = Resistor [tolerance=±5% resistance=280 package=THT]
  Default = LED - 5mm [color="Red (633nm)" package="5 mm [THT]"]
  R2 = Resistor [tolerance=±5% resistance=280 package=THT]
  Speed_High = LED - 5mm [color="Green (555nm)" package="5 mm [THT]"]
  R3 = Resistor [tolerance=±5% resistance=280 package=THT]
  Speed_Medium = LED - 5mm [color="Green (555nm)" package="5 mm [THT]"]
  R4 = Resistor [tolerance=±5% resistance=280 package=THT]
  Speed_Low = LED - 5mm [color="Green (555nm)" package="5 mm [THT]"]
  R5 = Resistor [tolerance=±5% resistance=280 package=THT]
  Alarm_Can_Full = LED - 5mm [color="Blue (525nm)" package="5 mm [THT]"]
  R6 = Resistor [tolerance=±5% resistance=280 package=THT]
  Reset = Pushbutton [package="[THT]"]
  STOP = Pushbutton [package="[THT]"]
  Speed_Adjust = Rotary Potentiometer (Small) [maximum_resistance=10kΩ package=THT]
  IR1 = TSOP4838 [package=THT]
  START = Pushbutton [package="[THT]"]
  Speed_Select = Pushbutton [package="[THT]"]
  J1 = female pin header, 3 pins [form="♀ (female)"]
  J2 = female pin header, 3 pins [form="♀ (female)"]
  Logique = female pin header, 5 pins [form="♀ (female)"]

nets:
  N1: Nano_Motor_Drive.RESET, Reset.Pin_2
  GND: Nano_Motor_Drive.GND, Power.pin2, OK.cathode, Default.cathode, Speed_High.cathode, Speed_Medium.cathode, Speed_Low.cathode, Alarm_Can_Full.cathode, Reset.Pin_3, Reset.Pin_4, STOP.Pin_1, STOP.Pin_2, Speed_Adjust.leg1, IR1.GND, START.Pin_1, START.Pin_2, Speed_Select.Pin_1, Speed_Select.Pin_2
  N2: Nano_Motor_Drive.D2, Logique.pin3
  N3: Nano_Motor_Drive.D3, J1.pin1
  N4: Nano_Motor_Drive.D4, IR1.Out
  N5: Nano_Motor_Drive.D5, Logique.pin2
  N6: Nano_Motor_Drive.D6, Speed_Select.Pin_3, Speed_Select.Pin_4
  N7: Nano_Motor_Drive.D7, R3.Pin_0
  N8: Nano_Motor_Drive.D8, R4.Pin_0
  N9: Nano_Motor_Drive.D9, R5.Pin_0
  N10: Nano_Motor_Drive.D10, R6.Pin_0
  N11: Nano_Motor_Drive.D11/MOSI, R2.Pin_0
  N12: Nano_Motor_Drive.5V, Power.pin1, Speed_Adjust.leg2, Logique.pin1
  N13: Nano_Motor_Drive.A6, J2.pin1
  N14: Nano_Motor_Drive.A5, START.Pin_3, START.Pin_4
  N15: Nano_Motor_Drive.A4, STOP.Pin_3, STOP.Pin_4
  N16: Nano_Motor_Drive.A3, Logique.pin4
  N17: Nano_Motor_Drive.A2, Speed_Adjust.wiper
  3V3: Nano_Motor_Drive.3V3, IR1.Vcc
  N18: Nano_Motor_Drive.D12/MISO, R1.Pin_0
  N19: OK.anode, R1.Pin_1
  N20: Default.anode, R2.Pin_1
  N21: Speed_High.anode, R3.Pin_1
  N22: Speed_Medium.anode, R4.Pin_1
  N23: Speed_Low.anode, R5.Pin_1
  N24: Alarm_Can_Full.anode, R6.Pin_1

notes:
  5V
  GND
  Motor TRIAC A3
  Power relay D5
  Zero cross   D2
  Bidon Alarm D3
  +5V
  0V
  A3
  D5
  D2
  D3
  A6
  Can Full Sensor
  Tacho Pulse

custom parts:
  TSOP4838: The TSOP3848 are miniaturized receivers for infrared remote control systems. A PIN diode and a preamplifier are assembled on a lead frame, the epoxy package acts as an IR filter. The demodulated output signal can be directly decoded by a microprocessor. The TSOP4838 is compatible with all common IR remote control data formats.
